// Logisim project mult4x4.circ as structural Verilog
module mult4x4 (
  input  [3:0] A,
  input  [3:0] B,
  output [7:0] SUM1,
  output [7:0] SUM2,
  output [7:0] PRODUTO
);

  wire [3:0] and_1_out;
  wire [4:1] and_5_out;
  wire [5:2] and_9_out;
  wire [6:3] and_13_out;

  and and_1 (and_1_out[0], A[0], B[0]);
  and and_2 (and_1_out[1], A[1], B[0]);
  and and_3 (and_1_out[2], A[3], B[0]);
  and and_4 (and_1_out[3], A[3], B[0]);
  and and_5 (and_5_out[1], A[0], B[1]);
  and and_6 (and_5_out[2], A[1], B[1]);
  and and_7 (and_5_out[3], A[3], B[1]);
  and and_8 (and_5_out[4], A[3], B[1]);
  and and_9 (and_9_out[2], A[0], B[2]);
  and and_10 (and_9_out[3], A[1], B[2]);
  and and_11 (and_9_out[4], A[3], B[2]);
  and and_12 (and_9_out[5], A[3], B[2]);
  and and_13 (and_13_out[3], A[0], B[3]);
  and and_14 (and_13_out[4], A[1], B[3]);
  and and_15 (and_13_out[5], A[3], B[3]);
  and and_16 (and_13_out[6], A[3], B[3]);
  Adder adder_1 (.a({4'b0000, and_1_out}), .b({3'b000, and_5_out, 1'b0}), .out(SUM1));  // open: cin, cout
  Adder adder_2 (.a(SUM1), .b({2'b00, and_9_out, 2'b00}), .out(SUM2));  // open: cin, cout
  Adder adder_3 (.a(SUM2), .b({1'b0, and_13_out, 3'b000}), .out(PRODUTO));  // open: cin, cout

  assign A[2] = A[3];
endmodule
