// Logisim project Somador.circ as structural Verilog
module meio_somador (
  input  BIT_A,
  input  BIT_B,
  output SOMA,
  output Cout
);

  xor xor_1 (SOMA, BIT_A, BIT_B);
  and and_1 (Cout, BIT_A, BIT_B);
endmodule

module Somador_completo (
  input  A,
  input  B,
  input  Cin,
  output Soma,
  output Cout
);

  wire AND1_out, AND2_out, XOR1_out;

  xor XOR1 (XOR1_out, A, B);
  and AND1 (AND1_out, A, B);
  xor XOR2 (Soma, XOR1_out, Cin);
  and AND2 (AND2_out, XOR1_out, Cin);
  or OR (Cout, AND1_out, AND2_out);
endmodule

module Somador_4_bits (
  input  Cin,
  input  [3:0] A,
  input  [3:0] B,
  output [3:0] SOMA,
  output Cout
);

  Adder #(.width(4)) adder_1 (.a(A), .b(B), .out(SOMA), .cin(Cin), .cout(Cout));
endmodule
