// Logisim project relogio.circ as structural Verilog: 6 circuits, main circuit main
module main (
  input  AM_PM_24H
);

  wire _0a59_2_clk_proximo, _0a59_clk_proximo, clock_1_out;
  wire [3:0] _0a59_2_dezena, _0a59_2_unidade, _0a59_dezena, _0a59_unidade, _12a12_24a0_dezena,
       _12a12_24a0_unidade;

  Hex_Digit_Display hex_digit_display_1 (.value(_12a12_24a0_dezena));  // open: dp
  Hex_Digit_Display hex_digit_display_2 (.value(_12a12_24a0_unidade));  // open: dp
  am_pm_24h _12a12_24a0 (
    .AM_PM(AM_PM_24H), .Dezena(_12a12_24a0_dezena), .Unidade(_12a12_24a0_unidade), .CLK(_0a59_clk_proximo));
  Hex_Digit_Display hex_digit_display_3 (.value(_0a59_dezena));  // open: dp
  Hex_Digit_Display hex_digit_display_4 (.value(_0a59_2_dezena));  // open: dp
  Hex_Digit_Display hex_digit_display_5 (.value(_0a59_unidade));  // open: dp
  _0a59 _0a59 (
    .CLK_PROXIMO(_0a59_clk_proximo), .DEZENA(_0a59_dezena), .UNIDADE(_0a59_unidade), .CLK(_0a59_2_clk_proximo));  // open: RESET
  Hex_Digit_Display hex_digit_display_6 (.value(_0a59_2_unidade));  // open: dp
  _0a59 _0a59_2 (
    .CLK_PROXIMO(_0a59_2_clk_proximo), .DEZENA(_0a59_2_dezena), .UNIDADE(_0a59_2_unidade), .CLK(clock_1_out));  // open: RESET
  Clock clock_1 (.out(clock_1_out));
endmodule

module _0a9 (
  input  CLK,
  input  RESET,
  output [3:0] saida,
  output CLK_PROXIMO
);

  wire OR_out;
  wire [3:0] adder_1_out;

  Register #(.width(4)) register_1 (.D(adder_1_out), .Q(saida), .clk(CLK), .clr(OR_out));  // open: en
  or OR (OR_out, CLK_PROXIMO, RESET);
  Hex_Digit_Display hex_digit_display_1 (.value(saida));  // open: dp
  Adder #(.width(4)) adder_1 (.a(saida), .b(4'b0001), .out(adder_1_out));  // open: cin, cout
  nor NOR (CLK_PROXIMO, saida[0], ~saida[1], saida[2], ~saida[3]);  // NOR_Gate
endmodule

module _0a59 (
  input  CLK,
  input  RESET,
  output [3:0] UNIDADE,
  output [3:0] DEZENA,
  output CLK_PROXIMO
);

  wire _0a9_2_clk_proximo, OR_out;

  Hex_Digit_Display hex_digit_display_1 (.value(DEZENA));  // open: dp
  _0a9 _0a9 (.CLK(_0a9_2_clk_proximo), .RESET(OR_out), .saida(DEZENA));  // open: CLK_PROXIMO
  nor NOR (CLK_PROXIMO, DEZENA[3], ~DEZENA[2], ~DEZENA[1], DEZENA[0], UNIDADE[3], UNIDADE[2], UNIDADE[1], UNIDADE[0]);  // NOR_Gate
  Hex_Digit_Display hex_digit_display_2 (.value(UNIDADE));  // open: dp
  _0a9 _0a9_2 (.CLK(CLK), .RESET(OR_out), .saida(UNIDADE), .CLK_PROXIMO(_0a9_2_clk_proximo));
  or OR (OR_out, CLK_PROXIMO, RESET);
endmodule

module _0a23 (
  input  CLK,
  input  RESET,
  output [3:0] UNIDADE,
  output [3:0] DEZENA,
  output CLK_PROXIMO
);

  wire _0a9_2_clk_proximo, OR_out;

  Hex_Digit_Display hex_digit_display_1 (.value(DEZENA));  // open: dp
  _0a9 _0a9 (.CLK(_0a9_2_clk_proximo), .RESET(OR_out), .saida(DEZENA));  // open: CLK_PROXIMO
  nor NOR (CLK_PROXIMO, DEZENA[3], DEZENA[2], ~DEZENA[1], DEZENA[0], UNIDADE[3], ~UNIDADE[2], UNIDADE[1], UNIDADE[0]);  // NOR_Gate
  Hex_Digit_Display hex_digit_display_2 (.value(UNIDADE));  // open: dp
  _0a9 _0a9_2 (.CLK(CLK), .RESET(OR_out), .saida(UNIDADE), .CLK_PROXIMO(_0a9_2_clk_proximo));
  or OR (OR_out, CLK_PROXIMO, RESET);
endmodule

module _12a12 (
  input  CLK,
  input  RESET,
  output [3:0] Dezena,
  output [3:0] Unidade
);

  wire _0a9_2_clk_proximo, NOR_2_out, NOR_out, OR_out;
  wire [3:0] _0a9_2_saida, _0a9_saida;

  Hex_Digit_Display hex_digit_display_1 (.value(Dezena));  // open: dp
  Multiplexer #(.width(4), .enable("false")) multiplexer_1 (
    .in0(_0a9_saida), .in1(4'b0001), .out(Dezena), .sel(NOR_2_out));
  _0a9 _0a9 (.CLK(_0a9_2_clk_proximo), .RESET(OR_out), .saida(_0a9_saida));  // open: CLK_PROXIMO
  nor NOR (NOR_out, _0a9_saida[3], _0a9_saida[2], _0a9_saida[1], ~_0a9_saida[0], _0a9_2_saida[3], _0a9_2_saida[2], ~_0a9_2_saida[1], _0a9_2_saida[0]);  // NOR_Gate
  Hex_Digit_Display hex_digit_display_2 (.value(Unidade));  // open: dp
  Multiplexer #(.width(4), .enable("false")) multiplexer_2 (
    .in0(_0a9_2_saida), .in1(4'b0010), .out(Unidade), .sel(NOR_2_out));
  _0a9 _0a9_2 (.CLK(CLK), .RESET(OR_out), .saida(_0a9_2_saida), .CLK_PROXIMO(_0a9_2_clk_proximo));
  or OR (OR_out, NOR_out, RESET);
  nor NOR_2 (NOR_2_out, _0a9_2_saida[0], _0a9_2_saida[1], _0a9_2_saida[2], _0a9_2_saida[3], _0a9_saida[0], _0a9_saida[1], _0a9_saida[2], _0a9_saida[3]);
endmodule

module am_pm_24h (
  input  AM_PM,
  input  CLK,
  output [3:0] Dezena,
  output [3:0] Unidade
);

  wire d_ff_1_q, subtractor_1_out;
  wire [3:0] _0a23_dezena, _0a23_unidade, _12a12_dezena, _12a12_unidade;

  D_Flip_Flop d_ff_1 (.clk(AM_PM), .D(subtractor_1_out), .Q(d_ff_1_q));  // open: Qn, preset, en, reset
  Subtractor #(.width(1)) subtractor_1 (.a(d_ff_1_q), .b(1'b1), .out(subtractor_1_out));  // open: bin, bout
  Hex_Digit_Display hex_digit_display_1 (.value(Dezena));  // open: dp
  Multiplexer #(.width(4), .enable("false")) multiplexer_1 (
    .in0(_0a23_dezena), .in1(_12a12_dezena), .out(Dezena), .sel(d_ff_1_q));
  _0a23 _0a23 (.DEZENA(_0a23_dezena), .UNIDADE(_0a23_unidade), .CLK(CLK));  // open: CLK_PROXIMO, RESET
  Hex_Digit_Display hex_digit_display_2 (.value(Unidade));  // open: dp
  Multiplexer #(.width(4), .enable("false")) multiplexer_2 (
    .in0(_0a23_unidade), .in1(_12a12_unidade), .out(Unidade), .sel(d_ff_1_q));
  _12a12 _12a12 (.Dezena(_12a12_dezena), .Unidade(_12a12_unidade), .CLK(CLK));  // open: RESET
endmodule
